// Logisim project jurassic_cpu.circ as structural Verilog: 3 circuits, main circuit main
module main (
  output [7:0] out_1,
  output [7:0] out_2,
  output [7:0] out_3
);

  wire and_1_out, and_2_out, and_3_out, clock_1_out, not_1_out, not_2_out, theClock_out;
  wire [3:0] decoder_1_out0;
  wire [7:0] adder_1_out, adder_2_out, datamemory_dout, multiplexer_1_out, multiplexer_2_out,
       multiplexer_3_out, multiplexer_4_out, multiplexer_5_out, multiplexer_6_out, PC_q, registers_1_q1,
       subtractor_1_out;
  wire [15:0] instructionMemory_dout;

  Adder adder_1 (.a(PC_q), .b(8'h1), .out(adder_1_out));  // open: cin, cout
  Clock theClock (.out(theClock_out));
  Register PC (.D(adder_1_out), .en(1'b1), .clk(theClock_out), .Q(PC_q));  // open: clr
  RAM #(.dataWidth(16), .enables("line")) instructionMemory (
    .addr(PC_q), .we(1'b0), .clk(theClock_out), .dout(instructionMemory_dout));  // open: din
  and and_1 (and_1_out, instructionMemory_dout[13], instructionMemory_dout[14]);
  not not_1 (not_1_out, and_1_out);
  Decoder #(.select(2)) decoder_1 (
    .out0(decoder_1_out0[0]), .out1(decoder_1_out0[1]), .out2(decoder_1_out0[2]), .out3(decoder_1_out0[3]),
    .sel(instructionMemory_dout[11:10]));  // open: en
  LedBar ledbar_1 (
    .led0(registers_1_q1[7]), .led1(registers_1_q1[6]), .led2(registers_1_q1[5]), .led3(registers_1_q1[4]),
    .led4(registers_1_q1[3]), .led5(registers_1_q1[2]), .led6(registers_1_q1[1]), .led7(registers_1_q1[0]));
  registers registers_1 (
    .clock(theClock_out), .D(multiplexer_6_out), .immReg(not_1_out), .decoder(decoder_1_out0),
    .Q1(registers_1_q1), .Q2(out_1), .Q3(out_2), .q4(out_3));
  Hex_Digit_Display hex_digit_display_1 (.value(multiplexer_6_out[7:4]));  // open: dp
  Multiplexer #(.select(2), .width(8)) multiplexer_1 (
    .in0(registers_1_q1), .in1(out_1), .in2(out_2), .in3(out_3), .out(multiplexer_1_out),
    .sel(instructionMemory_dout[1:0]));
  Multiplexer #(.select(2), .width(8)) multiplexer_2 (
    .in0(registers_1_q1), .in1(out_1), .in2(out_2), .in3(out_3), .out(multiplexer_2_out),
    .sel(instructionMemory_dout[9:8]));
  Hex_Digit_Display hex_digit_display_2 (.value(multiplexer_6_out[3:0]));  // open: dp
  Multiplexer #(.width(8)) multiplexer_3 (
    .in0(instructionMemory_dout[7:0]), .in1(multiplexer_1_out), .out(multiplexer_3_out),
    .sel(instructionMemory_dout[12]));
  and and_2 (and_2_out, instructionMemory_dout[13], instructionMemory_dout[14]);
  not not_2 (not_2_out, and_2_out);
  and and_3 (and_3_out, instructionMemory_dout[13], not_2_out);
  Adder adder_2 (.a(multiplexer_3_out), .b(multiplexer_2_out), .out(adder_2_out));  // open: cin, cout
  Multiplexer #(.width(8)) multiplexer_4 (
    .in0(adder_2_out), .in1(subtractor_1_out), .out(multiplexer_4_out), .sel(and_3_out));
  Subtractor subtractor_1 (.a(multiplexer_2_out), .b(multiplexer_3_out), .out(subtractor_1_out));  // open: bin, bout
  RAM #(.enables("line")) datamemory (
    .addr(multiplexer_4_out), .we(and_1_out), .clk(clock_1_out), .din(multiplexer_5_out),
    .dout(datamemory_dout));
  Clock clock_1 (.out(clock_1_out));
  Multiplexer #(.select(2), .width(8)) multiplexer_5 (
    .in0(registers_1_q1), .in1(out_1), .in2(out_2), .in3(out_3), .out(multiplexer_5_out),
    .sel(instructionMemory_dout[11:10]));
  Multiplexer #(.width(8)) multiplexer_6 (
    .in0(multiplexer_4_out), .in1(datamemory_dout), .out(multiplexer_6_out), .sel(instructionMemory_dout[14]));

  // Notes on the sheet:
  //   0-2:opcode
  //   3:imm/reg
  //   4-5:x0
  //   6-7:x1
  //   8-15:imm val
  //   J.U.R.A.S.S.I.C  CPU(Juxtaposed Universal Regulator Architecture System Supporting Integrated Computing)
  //   x1
  //   x0
  //   not
  //   reg1-4
  //   not
  //   ALU
  //   yes
  //   Arithmetic(ADD/SUB)
endmodule

module registers (
  input  clock,
  input  [7:0] D,
  input  immReg,
  input  [3:0] decoder,
  output [7:0] Q1,
  output [7:0] Q2,
  output [7:0] Q3,
  output [7:0] q4
);

  wire and_1_out, and_2_out, and_3_out, and_4_out;

  and and_1 (and_1_out, immReg, decoder[0]);
  and and_2 (and_2_out, immReg, decoder[1]);
  and and_3 (and_3_out, immReg, decoder[2]);
  and and_4 (and_4_out, immReg, decoder[3]);
  Register x0 (.D(D), .en(and_1_out), .clk(clock), .Q(Q1));  // open: clr
  Register x1 (.D(D), .en(and_2_out), .clk(clock), .Q(Q2));  // open: clr
  Register x2 (.D(D), .en(and_3_out), .clk(clock), .Q(Q3));  // open: clr
  Register x3 (.D(D), .en(and_4_out), .clk(clock), .Q(q4));  // open: clr
endmodule

module yuh (
  input  [3:0] in_1,
  output out_2,
  output out_3,
  output out_4,
  output out_5
);


  assign out_2 = in_1[0];
  assign out_3 = in_1[1];
  assign out_4 = in_1[2];
  assign out_5 = in_1[3];
endmodule
